// Logisim project OpenCPU.circ as structural Verilog: 7 circuits, main circuit FullAdder
module FullAdder (
  input  A,
  input  B,
  input  A1,
  input  B1,
  output Sum,
  output Carry
);

  HalfAdder HA1 (.A(A), .B(B), .A1(A1), .B1(B1), .Sum(Sum), .Carry(Carry));
endmodule

module HalfAdder (
  input  A,
  input  B,
  input  A1,
  input  B1,
  output Sum,
  output Carry
);

  xor xor_1 (Carry, A1, B1);
  and and_1 (Sum, A, B);
endmodule

module ALU (
  input  A,
  input  B,
  input  A1,
  input  B1,
  input  A2,
  input  B2,
  input  A3,
  input  B3,
  input  A4,
  input  B4,
  input  A5,
  input  B5,
  input  A6,
  input  B6,
  input  A7,
  input  B7,
  output R0,
  output R1,
  output R2,
  output R3
);

  wire ALU0_carry, ALU0_sum, ALU1_carry, ALU1_sum, ALU2_carry, ALU2_sum, ALU3_carry, ALU3_sum;

  FullAdder ALU0 (.A(A), .B(B), .A1(A1), .B1(B1), .Sum(ALU0_sum), .Carry(ALU0_carry));
  FullAdder ALU1 (.A(A2), .B(B2), .A1(A3), .B1(B3), .Sum(ALU1_sum), .Carry(ALU1_carry));
  FullAdder ALU2 (.A(A4), .B(B4), .A1(A5), .B1(B5), .Sum(ALU2_sum), .Carry(ALU2_carry));
  FullAdder ALU3 (.A(A6), .B(B6), .A1(A7), .B1(B7), .Sum(ALU3_sum), .Carry(ALU3_carry));
  Multiplexer multiplexer_1 (.in0(ALU0_sum), .in1(ALU0_carry), .out(R0), .sel(1'b1));
  Multiplexer multiplexer_2 (.in0(ALU1_sum), .in1(ALU1_carry), .out(R1), .sel(1'b1));
  Multiplexer multiplexer_3 (.in0(ALU2_sum), .in1(ALU2_carry), .out(R2), .sel(1'b1));
  Multiplexer multiplexer_4 (.in0(ALU3_sum), .in1(ALU3_carry), .out(R3), .sel(1'b1));
endmodule

module CPU (
  input  in_1,
  input  in_2,
  input  in_3,
  input  in_4,
  input  in_5,
  input  in_6,
  input  in_7,
  input  in_8,
  input  in_9,
  input  in_10,
  input  in_11,
  input  in_12,
  input  in_13,
  input  in_14,
  input  in_15,
  input  in_16,
  output out_17
);

  wire alu_1_r0, alu_1_r1, alu_1_r2, alu_1_r3, button_1_out, button_2_out, button_3_out, button_4_out,
       button_5_out, clock_1_out, controlunit_b_1_add_outp, controlunit_b_1_sub_outp, or_1_out, register_1_q,
       register_2_q, register_3_q, register_4_q, we_auto_enable_1_outp, we_auto_enable_2_outp,
       we_auto_enable_3_outp, we_auto_enable_4_outp;
  wire [3:0] controlunit_a_1_outp;

  ALU alu_1 (
    .A(in_1), .B(in_2), .A1(in_3), .B1(in_4), .A2(in_5), .B2(in_6), .A3(in_7), .B3(in_8), .A4(in_9),
    .B4(in_10), .A5(in_11), .B5(in_12), .A6(in_13), .B6(in_14), .A7(in_15), .B7(in_16), .R0(alu_1_r0),
    .R1(alu_1_r1), .R2(alu_1_r2), .R3(alu_1_r3));
  WE_Auto_Enable we_auto_enable_1 (.inp(alu_1_r0), .outp(we_auto_enable_1_outp));
  Register #(.width(1)) register_1 (
    .D(alu_1_r0), .en(we_auto_enable_1_outp), .clk(clock_1_out), .Q(register_1_q), .clr(button_1_out));
  Button button_1 (.out(button_1_out));
  WE_Auto_Enable we_auto_enable_2 (.inp(alu_1_r3), .outp(we_auto_enable_2_outp));
  Register #(.width(1)) register_2 (
    .D(alu_1_r1), .en(we_auto_enable_3_outp), .clk(clock_1_out), .Q(register_2_q), .clr(button_3_out));
  WE_Auto_Enable we_auto_enable_3 (.inp(alu_1_r1), .outp(we_auto_enable_3_outp));
  Register #(.width(1)) register_3 (
    .D(alu_1_r3), .en(we_auto_enable_2_outp), .clk(clock_1_out), .Q(register_3_q), .clr(button_2_out));
  Button button_2 (.out(button_2_out));
  Clock clock_1 (.out(clock_1_out));
  WE_Auto_Enable we_auto_enable_4 (.inp(alu_1_r2), .outp(we_auto_enable_4_outp));
  Button button_3 (.out(button_3_out));
  Register #(.width(1)) register_4 (
    .D(alu_1_r2), .en(we_auto_enable_4_outp), .clk(clock_1_out), .Q(register_4_q), .clr(button_4_out));
  Button button_4 (.out(button_4_out));
  ControlUnit_A controlunit_a_1 (.inp(register_1_q), .outp(controlunit_a_1_outp[0]));
  ControlUnit_A controlunit_a_2 (.inp(register_2_q), .outp(controlunit_a_1_outp[1]));
  ControlUnit_A controlunit_a_3 (.inp(register_3_q), .outp(controlunit_a_1_outp[2]));
  ControlUnit_A controlunit_a_4 (.inp(register_4_q), .outp(controlunit_a_1_outp[3]));
  ControlUnit_B controlunit_b_1 (
    .in_1(controlunit_a_1_outp), .out_2(out_17), .ADD_outp(controlunit_b_1_add_outp),
    .SUB_outp(controlunit_b_1_sub_outp));
  or or_1 (or_1_out, controlunit_b_1_add_outp, controlunit_b_1_sub_outp);
  Register #(.width(1)) register_5 (.D(or_1_out), .en(1'b1), .clk(clock_1_out), .clr(button_5_out));  // open: Q
  Button button_5 (.out(button_5_out));
endmodule

module WE_Auto_Enable (
  input  inp,
  output outp
);


  assign outp = inp;
endmodule

module ControlUnit_A (
  input  inp,
  output outp
);

  wire decoder_1_out1;

  Decoder #(.enable("false")) decoder_1 (.out0(outp), .out1(decoder_1_out1), .sel(inp));
endmodule

module ControlUnit_B (
  input  [3:0] in_1,
  output out_2,
  output ADD_outp,
  output SUB_outp
);

  Decoder #(.enable("false"), .select(4)) decoder_1 (
    .out0(out_2), .out1(ADD_outp), .out2(SUB_outp), .sel(in_1));  // open: out3, out4, out5, out6, out7, out8, out9, out10, out11, out12, out13, out14, out15
endmodule
