// Logisim project OpenCPU_8B.circ as structural Verilog: 7 circuits, main circuit FullAdder
module FullAdder (
  input  A,
  input  B,
  input  A1,
  input  B1,
  input  A2,
  input  B2,
  input  A3,
  input  B3,
  output Sum,
  output Carry,
  output Sum1,
  output Carry1
);

  HalfAdder halfadder_1 (.A(A2), .B(B2), .A1(A3), .B1(B3), .Sum(Sum1), .Carry(Carry1));
  HalfAdder halfadder_2 (.A(A), .B(B), .A1(A1), .B1(B1), .Sum(Sum), .Carry(Carry));
endmodule

module HalfAdder (
  input  A,
  input  B,
  input  A1,
  input  B1,
  output Sum,
  output Carry
);

  xor xor_1 (Carry, A1, B1);
  and and_1 (Sum, A, B);
endmodule

module ALU (
  input  A,
  input  B,
  input  A1,
  input  B1,
  input  A2,
  input  B2,
  input  A3,
  input  B3,
  input  A4,
  input  B4,
  input  A5,
  input  B5,
  input  A6,
  input  B6,
  input  A7,
  input  B7,
  input  in_17,
  input  in_18,
  input  in_19,
  input  in_20,
  input  in_21,
  input  in_22,
  input  in_23,
  input  in_24,
  input  in_25,
  input  in_26,
  input  in_27,
  input  in_28,
  input  in_29,
  input  in_30,
  input  in_31,
  input  in_32,
  input  in_33,
  input  in_34,
  input  in_35,
  input  in_36,
  input  in_37,
  input  in_38,
  input  in_39,
  input  in_40,
  input  in_41,
  input  in_42,
  input  in_43,
  input  in_44,
  input  in_45,
  input  in_46,
  input  in_47,
  input  in_48,
  input  in_49,
  input  in_50,
  input  in_51,
  input  in_52,
  input  in_53,
  input  in_54,
  input  in_55,
  input  in_56,
  input  in_57,
  input  in_58,
  input  in_59,
  input  in_60,
  input  in_61,
  input  in_62,
  input  in_63,
  input  in_64,
  input  in_65,
  input  in_66,
  input  in_67,
  input  in_68,
  input  in_69,
  input  in_70,
  input  in_71,
  input  in_72,
  input  in_73,
  input  in_74,
  input  in_75,
  input  in_76,
  input  in_77,
  input  in_78,
  input  in_79,
  input  in_80,
  output Y0,
  output out_82,
  output out_83,
  output out_84,
  output out_85,
  output out_86,
  output out_87,
  output out_88,
  output out_89,
  output out_90
);

  wire fulladder_1_carry, fulladder_1_carry1, fulladder_1_sum, fulladder_1_sum1, fulladder_2_carry,
       fulladder_2_carry1, fulladder_2_sum, fulladder_2_sum1, fulladder_3_carry, fulladder_3_carry1,
       fulladder_3_sum, fulladder_3_sum1, fulladder_4_carry, fulladder_4_carry1, fulladder_4_sum,
       fulladder_4_sum1, fulladder_5_carry, fulladder_5_carry1, fulladder_5_sum, fulladder_5_sum1,
       fulladder_6_carry, fulladder_6_carry1, fulladder_6_sum, fulladder_6_sum1, fulladder_7_carry,
       fulladder_7_carry1, fulladder_7_sum, fulladder_7_sum1, fulladder_8_carry, fulladder_8_carry1,
       fulladder_8_sum, fulladder_8_sum1, fulladder_9_carry, fulladder_9_carry1, fulladder_9_sum,
       fulladder_9_sum1, fulladder_10_carry, fulladder_10_carry1, fulladder_10_sum, fulladder_10_sum1;

  FullAdder fulladder_1 (
    .A(A), .B(B), .A1(A1), .B1(B1), .A2(A2), .B2(B2), .A3(A3), .B3(B3), .Sum(fulladder_1_sum),
    .Carry(fulladder_1_carry), .Sum1(fulladder_1_sum1), .Carry1(fulladder_1_carry1));
  FullAdder fulladder_2 (
    .A(A4), .B(B4), .A1(A5), .B1(B5), .A2(A6), .B2(B6), .A3(A7), .B3(B7), .Sum(fulladder_2_sum),
    .Carry(fulladder_2_carry), .Sum1(fulladder_2_sum1), .Carry1(fulladder_2_carry1));
  FullAdder fulladder_3 (
    .A(in_17), .B(in_18), .A1(in_19), .B1(in_20), .A2(in_21), .B2(in_22), .A3(in_23), .B3(in_24),
    .Sum(fulladder_3_sum), .Carry(fulladder_3_carry), .Sum1(fulladder_3_sum1), .Carry1(fulladder_3_carry1));
  FullAdder fulladder_4 (
    .A(in_25), .B(in_26), .A1(in_27), .B1(in_28), .A2(in_29), .B2(in_30), .A3(in_31), .B3(in_32),
    .Sum(fulladder_4_sum), .Carry(fulladder_4_carry), .Sum1(fulladder_4_sum1), .Carry1(fulladder_4_carry1));
  FullAdder fulladder_5 (
    .A(in_33), .B(in_34), .A1(in_35), .B1(in_36), .A2(in_37), .B2(in_38), .A3(in_39), .B3(in_40),
    .Sum(fulladder_5_sum), .Carry(fulladder_5_carry), .Sum1(fulladder_5_sum1), .Carry1(fulladder_5_carry1));
  FullAdder fulladder_6 (
    .A(in_41), .B(in_42), .A1(in_43), .B1(in_44), .A2(in_45), .B2(in_46), .A3(in_47), .B3(in_48),
    .Sum(fulladder_6_sum), .Carry(fulladder_6_carry), .Sum1(fulladder_6_sum1), .Carry1(fulladder_6_carry1));
  FullAdder fulladder_7 (
    .A(in_49), .B(in_50), .A1(in_51), .B1(in_52), .A2(in_53), .B2(in_54), .A3(in_55), .B3(in_56),
    .Sum(fulladder_7_sum), .Carry(fulladder_7_carry), .Sum1(fulladder_7_sum1), .Carry1(fulladder_7_carry1));
  FullAdder fulladder_8 (
    .A(in_57), .B(in_58), .A1(in_59), .B1(in_60), .A2(in_61), .B2(in_62), .A3(in_63), .B3(in_64),
    .Sum(fulladder_8_sum), .Carry(fulladder_8_carry), .Sum1(fulladder_8_sum1), .Carry1(fulladder_8_carry1));
  FullAdder fulladder_9 (
    .A(in_65), .B(in_66), .A1(in_67), .B1(in_68), .A2(in_69), .B2(in_70), .A3(in_71), .B3(in_72),
    .Sum(fulladder_9_sum), .Carry(fulladder_9_carry), .Sum1(fulladder_9_sum1), .Carry1(fulladder_9_carry1));
  FullAdder fulladder_10 (
    .A(in_73), .B(in_74), .A1(in_75), .B1(in_76), .A2(in_77), .B2(in_78), .A3(in_79), .B3(in_80),
    .Sum(fulladder_10_sum), .Carry(fulladder_10_carry), .Sum1(fulladder_10_sum1), .Carry1(fulladder_10_carry1));
  Multiplexer #(.select(2)) multiplexer_1 (
    .in0(fulladder_1_sum), .in1(fulladder_1_carry), .in2(fulladder_1_sum1), .in3(fulladder_1_carry1),
    .out(Y0), .sel(2'b11));
  Multiplexer #(.select(2)) multiplexer_2 (
    .in0(fulladder_2_sum), .in1(fulladder_2_carry), .in2(fulladder_2_sum1), .in3(fulladder_2_carry1),
    .out(out_82), .sel(2'b11));
  Multiplexer #(.select(2)) multiplexer_3 (
    .in0(fulladder_3_sum), .in1(fulladder_3_carry), .in2(fulladder_3_sum1), .in3(fulladder_3_carry1),
    .out(out_83), .sel(2'b11));
  Multiplexer #(.select(2)) multiplexer_4 (
    .in0(fulladder_4_sum), .in1(fulladder_4_carry), .in2(fulladder_4_sum1), .in3(fulladder_4_carry1),
    .out(out_84), .sel(2'b11));
  Multiplexer #(.select(2)) multiplexer_5 (
    .in0(fulladder_5_sum), .in1(fulladder_5_carry), .in2(fulladder_5_sum1), .in3(fulladder_5_carry1),
    .out(out_85), .sel(2'b11));
  Multiplexer #(.select(2)) multiplexer_6 (
    .in0(fulladder_6_sum), .in1(fulladder_6_carry), .in2(fulladder_6_sum1), .in3(fulladder_6_carry1),
    .out(out_86), .sel(2'b11));
  Multiplexer #(.select(2)) multiplexer_7 (
    .in0(fulladder_7_sum), .in1(fulladder_7_carry), .in2(fulladder_7_sum1), .in3(fulladder_7_carry1),
    .out(out_87), .sel(2'b11));
  Multiplexer #(.select(2)) multiplexer_8 (
    .in0(fulladder_8_sum), .in1(fulladder_8_carry), .in2(fulladder_8_sum1), .in3(fulladder_8_carry1),
    .out(out_88), .sel(2'b11));
  Multiplexer #(.select(2)) multiplexer_9 (
    .in0(fulladder_9_sum), .in1(fulladder_9_carry), .in2(fulladder_9_sum1), .in3(fulladder_9_carry1),
    .out(out_89), .sel(2'b11));
  Multiplexer #(.select(2)) multiplexer_10 (
    .in0(fulladder_10_sum), .in1(fulladder_10_carry), .in2(fulladder_10_sum1), .in3(fulladder_10_carry1),
    .out(out_90), .sel(2'b11));
endmodule

module CPU (
  input  in_1,
  input  in_2,
  input  in_3,
  input  in_4,
  input  in_5,
  input  in_6,
  input  in_7,
  input  in_8,
  input  in_9,
  input  in_10,
  input  in_11,
  input  in_12,
  input  in_13,
  input  in_14,
  input  in_15,
  input  in_16,
  input  in_17,
  input  in_18,
  input  in_19,
  input  in_20,
  input  in_21,
  input  in_22,
  input  in_23,
  input  in_24,
  input  in_25,
  input  in_26,
  input  in_27,
  input  in_28,
  input  in_29,
  input  in_30,
  input  in_31,
  input  in_32,
  input  in_33,
  input  in_34,
  input  Outp,
  input  in_36,
  input  in_37,
  input  in_38,
  input  in_39,
  input  in_40,
  input  in_41,
  input  in_42,
  input  in_43,
  input  in_44,
  input  in_45,
  input  in_46,
  input  in_47,
  input  in_48,
  input  in_49,
  input  in_50,
  input  in_51,
  input  in_52,
  input  in_53,
  input  in_54,
  input  in_55,
  input  in_56,
  input  in_57,
  input  in_58,
  input  in_59,
  input  in_60,
  input  in_61,
  input  in_62,
  input  in_63,
  input  in_64,
  input  in_65,
  input  in_66,
  input  in_67,
  input  in_68,
  input  in_69,
  input  in_70,
  input  in_71,
  input  in_72,
  input  in_73,
  input  in_74,
  input  in_75,
  input  in_76,
  input  in_77,
  input  in_78,
  input  in_79,
  input  in_80,
  input  in_81,
  output out_82
);

  wire alu_1_out_82, alu_1_out_83, alu_1_out_84, alu_1_out_85, alu_1_out_86, alu_1_out_87, alu_1_out_88,
       alu_1_out_89, alu_1_out_90, alu_1_y0, button_1_out, button_2_out, button_3_out, button_4_out,
       button_5_out, button_6_out, button_7_out, button_8_out, button_9_out, button_10_out, button_11_out,
       clock_1_out, controlunit_b_1_add_outp, controlunit_b_1_sub_outp, or_1_out, register_3_q, register_4_q,
       register_5_q, register_6_q, register_7_q, register_10_q, we_auto_enable_1_outp, we_auto_enable_2_outp,
       we_auto_enable_3_outp, we_auto_enable_4_outp, we_auto_enable_5_outp, we_auto_enable_6_outp,
       we_auto_enable_7_outp, we_auto_enable_8_outp, we_auto_enable_9_outp, we_auto_enable_10_outp,
       we_auto_enable_11_outp;
  wire [3:0] register_1_q;

  ALU alu_1 (
    .A(in_1), .B(in_2), .A1(in_3), .B1(in_4), .A2(in_5), .B2(in_6), .A3(in_7), .B3(in_8), .A4(in_9),
    .B4(in_10), .A5(in_11), .B5(in_12), .A6(in_13), .B6(in_14), .A7(in_15), .B7(in_16), .in_17(in_17),
    .in_18(in_18), .in_19(in_19), .in_20(in_20), .in_21(in_21), .in_22(in_22), .in_23(in_23), .in_24(in_24),
    .in_25(in_25), .in_26(in_26), .in_27(in_27), .in_28(in_28), .in_29(in_29), .in_30(in_30), .in_31(in_31),
    .in_32(in_32), .in_33(in_33), .in_34(in_34), .in_35(in_36), .in_36(in_37), .in_37(in_38), .in_38(in_39),
    .in_39(in_40), .in_40(in_41), .in_41(in_42), .in_42(in_43), .in_43(in_44), .in_44(in_45), .in_45(in_46),
    .in_46(in_47), .in_47(in_48), .in_48(in_49), .in_49(in_50), .in_50(in_51), .in_51(in_52), .in_52(in_53),
    .in_53(in_54), .in_54(in_55), .in_55(in_56), .in_56(in_57), .in_57(in_58), .in_58(in_59), .in_59(in_60),
    .in_60(in_61), .in_61(in_62), .in_62(in_63), .in_63(in_64), .in_64(in_65), .in_65(in_66), .in_66(in_67),
    .in_67(in_68), .in_68(in_69), .in_69(in_70), .in_70(in_71), .in_71(in_72), .in_72(in_73), .in_73(in_74),
    .in_74(in_75), .in_75(in_76), .in_76(in_77), .in_77(in_78), .in_78(in_79), .in_79(in_80), .in_80(in_81),
    .Y0(alu_1_y0), .out_82(alu_1_out_82), .out_83(alu_1_out_83), .out_84(alu_1_out_84),
    .out_85(alu_1_out_85), .out_86(alu_1_out_86), .out_87(alu_1_out_87), .out_88(alu_1_out_88),
    .out_89(alu_1_out_89), .out_90(alu_1_out_90));
  Register #(.width(1)) register_1 (
    .D(alu_1_y0), .en(we_auto_enable_1_outp), .clk(clock_1_out), .Q(register_1_q[0]), .clr(button_1_out));
  WE_Auto_Enable we_auto_enable_1 (.inp(alu_1_y0), .outp(we_auto_enable_1_outp));
  Clock clock_1 (.out(clock_1_out));
  Button button_1 (.out(button_1_out));
  Register #(.width(1)) register_2 (
    .D(alu_1_out_82), .en(we_auto_enable_2_outp), .clk(clock_1_out), .Q(register_1_q[1]), .clr(button_4_out));
  WE_Auto_Enable we_auto_enable_2 (.inp(alu_1_out_82), .outp(we_auto_enable_2_outp));
  Register #(.width(1)) register_3 (
    .D(alu_1_out_85), .en(we_auto_enable_3_outp), .clk(clock_1_out), .Q(register_3_q), .clr(button_2_out));
  WE_Auto_Enable we_auto_enable_3 (.inp(alu_1_out_85), .outp(we_auto_enable_3_outp));
  Button button_2 (.out(button_2_out));
  Register #(.width(1)) register_4 (
    .D(alu_1_out_86), .en(we_auto_enable_4_outp), .clk(clock_1_out), .Q(register_4_q), .clr(button_3_out));
  WE_Auto_Enable we_auto_enable_4 (.inp(alu_1_out_86), .outp(we_auto_enable_4_outp));
  Button button_3 (.out(button_3_out));
  Register #(.width(1)) register_5 (
    .D(alu_1_out_88), .en(we_auto_enable_5_outp), .clk(clock_1_out), .Q(register_5_q), .clr(button_8_out));
  WE_Auto_Enable we_auto_enable_5 (.inp(alu_1_out_88), .outp(we_auto_enable_5_outp));
  Register #(.width(1)) register_6 (
    .D(alu_1_out_89), .en(we_auto_enable_6_outp), .clk(clock_1_out), .Q(register_6_q), .clr(button_9_out));
  WE_Auto_Enable we_auto_enable_6 (.inp(alu_1_out_89), .outp(we_auto_enable_6_outp));
  Register #(.width(1)) register_7 (
    .D(alu_1_out_90), .en(we_auto_enable_7_outp), .clk(clock_1_out), .Q(register_7_q), .clr(button_10_out));
  WE_Auto_Enable we_auto_enable_7 (.inp(alu_1_out_90), .outp(we_auto_enable_7_outp));
  Button button_4 (.out(button_4_out));
  Register #(.width(1)) register_8 (
    .D(alu_1_out_83), .en(we_auto_enable_8_outp), .clk(clock_1_out), .Q(register_1_q[2]), .clr(button_5_out));
  WE_Auto_Enable we_auto_enable_8 (.inp(alu_1_out_83), .outp(we_auto_enable_8_outp));
  Button button_5 (.out(button_5_out));
  Register #(.width(1)) register_9 (
    .D(alu_1_out_84), .en(we_auto_enable_9_outp), .clk(clock_1_out), .Q(register_1_q[3]), .clr(button_6_out));
  WE_Auto_Enable we_auto_enable_9 (.outp(we_auto_enable_9_outp));  // open: inp
  Button button_6 (.out(button_6_out));
  Register #(.width(1)) register_10 (
    .D(alu_1_out_87), .en(we_auto_enable_10_outp), .clk(clock_1_out), .Q(register_10_q), .clr(button_7_out));
  WE_Auto_Enable we_auto_enable_10 (.inp(alu_1_out_87), .outp(we_auto_enable_10_outp));
  Button button_7 (.out(button_7_out));
  Button button_8 (.out(button_8_out));
  Button button_9 (.out(button_9_out));
  Button button_10 (.out(button_10_out));
  ControlUnit_B controlunit_b_1 (
    .in_1(register_1_q), .out_2(out_82), .ADD_outp(controlunit_b_1_add_outp),
    .SUB_outp(controlunit_b_1_sub_outp));
  or or_1 (or_1_out, controlunit_b_1_add_outp, controlunit_b_1_sub_outp);
  Register #(.width(1)) register_11 (
    .D(or_1_out), .en(we_auto_enable_11_outp), .clk(clock_1_out), .Q(Outp), .clr(button_11_out));
  WE_Auto_Enable we_auto_enable_11 (.inp(or_1_out), .outp(we_auto_enable_11_outp));
  Button button_11 (.out(button_11_out));
endmodule

module WE_Auto_Enable (
  input  inp,
  output outp
);


  assign outp = inp;
endmodule

module ControlUnit_A (
  input  inp,
  output outp
);

  wire decoder_1_out1;

  Decoder #(.enable("false")) decoder_1 (.out0(outp), .out1(decoder_1_out1), .sel(inp));
endmodule

module ControlUnit_B (
  input  [3:0] in_1,
  output out_2,
  output ADD_outp,
  output SUB_outp
);

  Decoder #(.enable("false"), .select(4)) decoder_1 (
    .out0(out_2), .out1(ADD_outp), .out2(SUB_outp), .sel(in_1));  // open: out3, out4, out5, out6, out7, out8, out9, out10, out11, out12, out13, out14, out15
endmodule
